// Logisim project myAlu.circ as structural Verilog
module myNOT (
  input  in_1,
  output out_2
);

  nand nand_1 (out_2, in_1, in_1);
endmodule

module myAND (
  input  in_1,
  input  in_2,
  output out_3
);

  wire nand_1_out;

  nand nand_1 (nand_1_out, in_1, in_2);
  myNOT mynot_1 (.in_1(nand_1_out), .out_2(out_3));
endmodule

module myOR (
  input  in_1,
  input  in_2,
  output out_3
);

  wire mynot_1_out_2, mynot_2_out_2;

  myNOT mynot_1 (.in_1(in_1), .out_2(mynot_1_out_2));
  myNOT mynot_2 (.in_1(in_2), .out_2(mynot_2_out_2));
  nand nand_1 (out_3, mynot_1_out_2, mynot_2_out_2);
endmodule

module myXOR (
  input  in_1,
  input  in_2,
  output out_3
);

  wire myand_1_out_3, myand_2_out_3, mynot_1_out_2, mynot_2_out_2;

  myNOT mynot_1 (.in_1(in_1), .out_2(mynot_1_out_2));
  myNOT mynot_2 (.in_1(in_2), .out_2(mynot_2_out_2));
  myAND myand_1 (.in_1(mynot_1_out_2), .in_2(in_2), .out_3(myand_1_out_3));
  myAND myand_2 (.in_1(in_1), .in_2(mynot_2_out_2), .out_3(myand_2_out_3));
  myOR myor_1 (.in_1(myand_1_out_3), .in_2(myand_2_out_3), .out_3(out_3));
endmodule

module myMUX (
  input  A,
  input  B,
  input  in_3,
  output out_4
);

  wire myand_1_out_3, myand_2_out_3, mynot_1_out_2;

  myNOT mynot_1 (.in_1(in_3), .out_2(mynot_1_out_2));
  myAND myand_1 (.in_1(A), .in_2(mynot_1_out_2), .out_3(myand_1_out_3));
  myAND myand_2 (.in_1(B), .in_2(in_3), .out_3(myand_2_out_3));
  myXOR myxor_1 (.in_1(myand_1_out_3), .in_2(myand_2_out_3), .out_3(out_4));
endmodule

module myDMUX (
  input  in_1,
  input  in_2,
  output out_3,
  output out_4
);

  wire mynot_1_out_2;

  myNOT mynot_1 (.in_1(in_2), .out_2(mynot_1_out_2));
  myAND myand_1 (.in_1(in_1), .in_2(mynot_1_out_2), .out_3(out_3));
  myAND myand_2 (.in_1(in_1), .in_2(in_2), .out_3(out_4));
endmodule

module myHalfAdder (
  input  in_1,
  input  in_2,
  output S,
  output C
);

  myXOR myxor_1 (.in_1(in_1), .in_2(in_2), .out_3(S));
  myAND myand_1 (.in_1(in_1), .in_2(in_2), .out_3(C));
endmodule

module myFullAdder (
  input  in_1,
  input  A,
  input  B,
  output S,
  output C
);

  wire myhalfadder_1_c, myhalfadder_1_s, myhalfadder_2_c;

  myHalfAdder myhalfadder_1 (.in_1(A), .in_2(B), .S(myhalfadder_1_s), .C(myhalfadder_1_c));
  myHalfAdder myhalfadder_2 (.in_1(in_1), .in_2(myhalfadder_1_s), .S(S), .C(myhalfadder_2_c));
  myOR myor_1 (.in_1(myhalfadder_2_c), .in_2(myhalfadder_1_c), .out_3(C));
endmodule

module myALU (
  input  A,
  input  B,
  input  C,
  input  L,
  input  R,
  input  in_6,
  input  in_7,
  input  in_8,
  input  in_9,
  output out_10,
  output Cout
);

  wire myau_1_s, mylu_1_out_7, mymux_1_out_4, mysu_1_out_4;

  myAU myau_1 (.Cin(C), .A(A), .B(B), .in_4(in_6), .in_5(in_7), .S(myau_1_s), .Cout(Cout));  // open: in_6, in_7
  myLU mylu_1 (.A(A), .B(B), .S0(in_6), .S1(in_7), .S2(in_8), .S3(in_9), .out_7(mylu_1_out_7));
  mySU mysu_1 (.R(L), .L(R), .S0(in_6), .out_4(mysu_1_out_4));
  myMUX mymux_1 (.A(myau_1_s), .B(mylu_1_out_7), .in_3(in_7), .out_4(mymux_1_out_4));
  myMUX mymux_2 (.A(mymux_1_out_4), .B(mysu_1_out_4), .in_3(in_8), .out_4(out_10));
endmodule

module myLU (
  input  A,
  input  B,
  input  S0,
  input  S1,
  input  S2,
  input  S3,
  output out_7
);

  wire myand_1_out_3, myand_2_out_3, myand_3_out_3, mymux_1_out_4, mymux_2_out_4, mymux_3_out_4,
       mymux_4_out_4, mymux_5_out_4, mymux_6_out_4, mymux_7_out_4, mynot_1_out_2, mynot_2_out_2,
       mynot_3_out_2, mynot_4_out_2, myor_1_out_3, myxor_1_out_3, myxor_2_out_3;

  myAND myand_1 (.in_1(A), .in_2(B), .out_3(myand_1_out_3));
  myOR myor_1 (.in_1(A), .in_2(B), .out_3(myor_1_out_3));
  myXOR myxor_1 (.in_1(A), .in_2(B), .out_3(myxor_1_out_3));
  myNOT mynot_1 (.in_1(A), .out_2(mynot_1_out_2));
  myXOR myxor_2 (.in_1(A), .in_2(B), .out_3(myxor_2_out_3));
  myNOT mynot_2 (.in_1(A), .out_2(mynot_2_out_2));
  myNOT mynot_3 (.in_1(B), .out_2(mynot_3_out_2));
  myNOT mynot_4 (.in_1(myxor_2_out_3), .out_2(mynot_4_out_2));
  myAND myand_2 (.in_1(mynot_2_out_2), .in_2(B), .out_3(myand_2_out_3));
  myAND myand_3 (.in_1(A), .in_2(mynot_3_out_2), .out_3(myand_3_out_3));
  myMUX mymux_1 (.A(myand_1_out_3), .B(myor_1_out_3), .in_3(S0), .out_4(mymux_1_out_4));
  myMUX mymux_2 (.A(myxor_1_out_3), .B(mynot_1_out_2), .in_3(S0), .out_4(mymux_2_out_4));
  myMUX mymux_3 (.A(mynot_4_out_2), .B(myand_2_out_3), .in_3(S0), .out_4(mymux_3_out_4));
  myMUX mymux_4 (.A(myand_3_out_3), .B(A), .in_3(S0), .out_4(mymux_4_out_4));
  myMUX mymux_5 (.A(mymux_1_out_4), .B(mymux_2_out_4), .in_3(S1), .out_4(mymux_5_out_4));
  myMUX mymux_6 (.A(mymux_3_out_4), .B(mymux_4_out_4), .in_3(S1), .out_4(mymux_6_out_4));
  myMUX mymux_7 (.A(mymux_5_out_4), .B(mymux_6_out_4), .in_3(S2), .out_4(mymux_7_out_4));
  myMUX mymux_8 (.A(mymux_7_out_4), .B(B), .in_3(S3), .out_4(out_7));
endmodule

module myAU (
  input  Cin,
  input  A,
  input  B,
  input  in_4,
  input  in_5,
  input  in_6,
  input  in_7,
  output S,
  output Cout
);

  wire myand_1_out_3, myand_2_out_3, myand_3_out_3, myand_4_out_3, myand_5_out_3, myand_6_out_3,
       myand_7_out_3, myand_8_out_3, myand_9_out_3, myand_10_out_3, mynot_1_out_2, mynot_2_out_2,
       mynot_3_out_2, mynot_4_out_2, mynot_5_out_2, mynot_6_out_2, mynot_7_out_2, myor_1_out_3, myor_2_out_3,
       myor_3_out_3, myor_4_out_3, myor_5_out_3, myor_6_out_3, myxor_1_out_3, myxor_2_out_3;

  myOR myor_1 (.in_1(B), .in_2(myand_1_out_3), .out_3(myor_1_out_3));
  myAND myand_1 (.in_1(myand_2_out_3), .in_2(myand_7_out_3), .out_3(myand_1_out_3));
  myAND myand_2 (.in_1(in_6), .in_2(in_7), .out_3(myand_2_out_3));
  myAND myand_3 (.in_1(myand_4_out_3), .in_2(myand_5_out_3), .out_3(myand_3_out_3));
  myAND myand_4 (.in_1(in_5), .in_2(mynot_1_out_2), .out_3(myand_4_out_3));
  myAND myand_5 (.in_1(mynot_2_out_2), .in_2(mynot_3_out_2), .out_3(myand_5_out_3));
  myNOT mynot_1 (.in_1(in_4), .out_2(mynot_1_out_2));
  myNOT mynot_2 (.in_1(in_6), .out_2(mynot_2_out_2));
  myNOT mynot_3 (.in_1(in_7), .out_2(mynot_3_out_2));
  myOR myor_2 (.in_1(myor_1_out_3), .in_2(myand_3_out_3), .out_3(myor_2_out_3));
  myOR myor_3 (.in_1(myand_3_out_3), .in_2(myand_6_out_3), .out_3(myor_3_out_3));
  myAND myand_6 (.in_1(myand_7_out_3), .in_2(myand_8_out_3), .out_3(myand_6_out_3));
  myAND myand_7 (.in_1(mynot_4_out_2), .in_2(mynot_5_out_2), .out_3(myand_7_out_3));
  myNOT mynot_4 (.in_1(in_4), .out_2(mynot_4_out_2));
  myOR myor_4 (.in_1(myand_3_out_3), .in_2(myor_5_out_3), .out_3(myor_4_out_3));
  myOR myor_5 (.in_1(myand_6_out_3), .in_2(myand_9_out_3), .out_3(myor_5_out_3));
  myAND myand_8 (.in_1(mynot_6_out_2), .in_2(in_7), .out_3(myand_8_out_3));
  myNOT mynot_5 (.in_1(in_5), .out_2(mynot_5_out_2));
  myNOT mynot_6 (.in_1(in_6), .out_2(mynot_6_out_2));
  myAND myand_9 (.in_1(myand_7_out_3), .in_2(myand_10_out_3), .out_3(myand_9_out_3));
  myAND myand_10 (.in_1(in_6), .in_2(mynot_7_out_2), .out_3(myand_10_out_3));
  myNOT mynot_7 (.in_1(in_7), .out_2(mynot_7_out_2));
  myOR myor_6 (.in_1(Cin), .in_2(myor_4_out_3), .out_3(myor_6_out_3));
  myXOR myxor_1 (.in_1(A), .in_2(myand_9_out_3), .out_3(myxor_1_out_3));
  myXOR myxor_2 (.in_1(myor_2_out_3), .in_2(myor_3_out_3), .out_3(myxor_2_out_3));
  myFullAdder myfulladder_1 (.in_1(myor_6_out_3), .A(myxor_1_out_3), .B(myxor_2_out_3), .S(S), .C(Cout));
endmodule

module mySU (
  input  R,
  input  L,
  input  S0,
  output out_4
);

  myMUX mymux_1 (.A(R), .B(L), .in_3(S0), .out_4(out_4));
endmodule
